# Fritzing sketch Esquematico (saved by Fritzing 1.0.1rc)

parts:
  Part1 = Arduino Uno (Rev3) - ICSP  # not connected
  MFS1 = Multi Function Shield
  RY1 = SSR-FOTEK [part_number=SSR-40DA-FOTEK]
  P1 = DS18B20 Probe
  J1 = 220v plug  # not connected
  J2 = 120V duplex outlet_1  # not connected

nets:
  N1: MFS1.GND#92, MFS1.GND#105, P1.GND
  N2: MFS1.GND#101, MFS1.GND#107, RY1.Pin_4
  N3: MFS1.J1-A4, P1.Sig
  VCC: MFS1.VCC, P1.VCC
  N4: MFS1.5, RY1.Pin_3

custom parts:
  Multi Function Shield: Das Multi Function Shield kann auf den Arduino Uno aufgesteckt werden und bietet ein paar wichtige Bauteile.
  SSR-FOTEK: Solid State Relay, SSR-40DA Links: SSR-40DA Datasheet
  220v plug: Generic 220V AC plug.
  120V duplex outlet_1: 120V duplex outlet.
